# Fritzing sketch PCB_design (saved by Fritzing 0.9.3b)
circuit board: 9.906cm x 7.62cm

parts:
  LED2 = smd LED [color="Red (633nm)" package="0603 [SMD]"]
  LED1 = smd LED [color="Red (633nm)" package="0603 [SMD]"]
  LED0 = smd LED [color="Red (633nm)" package="0603 [SMD]"]
  CZ2 = Pushbutton [package="[SMD]"]
  Phase = Pushbutton [package="[SMD]"]
  Error = Pushbutton [package="[SMD]"]
  Hadamard = Pushbutton [package="[SMD]"]
  CZ1 = Pushbutton [package="[SMD]"]
  Measure = Pushbutton [package="[SMD]"]
  R4 = Resistor [tolerance=±5% resistance=220 package="0603 [SMD]"]
  R2 = Resistor [tolerance=±5% resistance=220 package="0603 [SMD]"]
  R3 = Resistor [tolerance=±5% resistance=220 package="0603 [SMD]"]
  R1 = Resistor [tolerance=±5% resistance=220 package="0603 [SMD]"]
  U2 = RJ45 Jack [package=rj45-8]
  LEDA = smd LED [color="Green (565nm)" package="0603 [SMD]"]
  U1 = RJ45 Jack [package=rj45-8]
  C = Ceramic Capacitor [capacitance=100nF package="0603 [SMD, multilayer]"]
  BAT = Battery Holders [package=battcom_20mm_pth]
  ATTiny4313 = ATTiny4313 [chip_label=IC package=SO(w)]

nets:
  N1: LED2.cathode, LED1.cathode, LED0.cathode, R1.Pin_1
  N2: LED2.anode, ATTiny4313.14
  N3: LED1.anode, ATTiny4313.15
  N4: LED0.anode, ATTiny4313.16
  N5: CZ2.Pin_1, CZ2.Pin_2, ATTiny4313.9
  N6: CZ2.Pin_3, CZ2.Pin_4, Phase.Pin_3, Phase.Pin_4, Error.Pin_3, Error.Pin_4, Hadamard.Pin_1, Hadamard.Pin_2, CZ1.Pin_1, CZ1.Pin_2, Measure.Pin_3, Measure.Pin_4, R2.Pin_1, R1.Pin_0, C.0, BAT.-, ATTiny4313.10
  N7: Phase.Pin_1, Phase.Pin_2, ATTiny4313.8
  N8: Error.Pin_1, Error.Pin_2, ATTiny4313.7
  N9: Hadamard.Pin_3, Hadamard.Pin_4, ATTiny4313.6
  N10: CZ1.Pin_3, CZ1.Pin_4, ATTiny4313.2
  N11: Measure.Pin_1, Measure.Pin_2, ATTiny4313.11
  N12: R4.Pin_0, U2.3
  N13: R4.Pin_1, ATTiny4313.4
  N14: R2.Pin_0, LEDA.cathode
  N15: R3.Pin_0, ATTiny4313.5
  N16: R3.Pin_1, U1.3
  N17: U2.1, ATTiny4313.3
  N18: U2.2, ATTiny4313.1
  N19: U2.4, C.1, BAT.+, ATTiny4313.20
  N20: U2.5, ATTiny4313.17
  N21: U2.6, ATTiny4313.19
  N22: U2.8, ATTiny4313.18
  N23: LEDA.anode, ATTiny4313.13
  N24: U1.1, ATTiny4313.12

notes:
  J2
  J1
  +
  -

custom parts:
  Pushbutton: A generic pushbutton.
  Battery Holders: Battery Holders Various common sizes : AA, AAA, 20mm coin cell and 12mm coin cell.
