# Fritzing sketch circuit (saved by Fritzing 0.9.3b)
stripboards: 1

parts:
  IC1 = IC, DIP package, 20 pins [chip_label=ATtiny261A]
  VCC1 = Battery
  S1 = Pushbutton [package="[THT]"]
  S2 = Pushbutton [package="[THT]"]
  S3 = Pushbutton [package="[THT]"]
  S4 = Pushbutton [package="[THT]"]
  S5 = Pushbutton [package="[THT]"]
  R1 = Resistor [tolerance=±5% resistance=220 package=THT]
  LED1 = LED - 3mm [color="Red (633nm)" package="3 mm [THT]"]
  LED2 = LED - 3mm [color="Red (633nm)" package="3 mm [THT]"]
  LED3 = LED - 3mm [color="Green (555nm)" package="3 mm [THT]"]
  R4 = Resistor [tolerance=±5% resistance=220 package=THT]
  R5 = Resistor [tolerance=±5% resistance=220 package=THT]
  C1 = Ceramic Capacitor [capacitance=100nF package="100 mil [THT, multilayer]"]
  J1 = male pin header, 5 pins [form="♂ (male)"]

nets:
  N1: IC1.pin1, J1.pin1
  N2: IC1.pin2, J1.pin2
  N3: IC1.pin3, J1.pin3
  N4: IC1.pin5, VCC1.+, C1.0
  N5: IC1.pin6, VCC1.-, S1.Pin_1, S1.Pin_2, S2.Pin_3, S2.Pin_4, S3.Pin_3, S3.Pin_4, S4.Pin_3, S4.Pin_4, S5.Pin_3, S5.Pin_4, LED1.cathode, LED2.cathode, LED3.anode, C1.1
  N6: IC1.pin7, R1.Pin_0
  N7: IC1.pin8, R4.Pin_0
  N8: IC1.pin9, R5.Pin_0
  N9: IC1.pin10, J1.pin4
  N10: IC1.pin11, S1.Pin_3, S1.Pin_4
  N11: IC1.pin17, S4.Pin_1, S4.Pin_2
  N12: IC1.pin18, S2.Pin_1, S2.Pin_2
  N13: IC1.pin19, S5.Pin_1, S5.Pin_2
  N14: IC1.pin20, S3.Pin_1, S3.Pin_2
  N15: R1.Pin_1, LED1.anode
  N16: LED2.anode, R4.Pin_1
  N17: LED3.cathode, R5.Pin_1
